# Fritzing sketch Tornado-v2 (saved by Fritzing 0.9.3b)
breadboards: 1

parts:
  Part1 = Arduino Nano (Rev3.0) (ICSP)
  IC2 = L293D [package=THT]
  R2 = Rotary Potentiometer (Large) [maximum_resistance=100kΩ package=THT]
  M2 = DC Motor
  S4 = Pushbutton [package="[THT]"]
  R3 = Resistor [tolerance=±5% resistance=220 package=THT]
  U3 = LIPO-110mAh [package=lipo-110]
  S5 = Round Pushbutton
  U4 = 7-SEGMENT-4DIGIT [package=7-segment-4digit]

nets:
  N1: Part1.GND, IC2.0V, R2.leg2, R3.Pin_1, U3.-, U4.1
  N2: Part1.D2, S4.Pin_1, S4.Pin_2, R3.Pin_0
  N3: Part1.D3, IC2.Enable_2
  N4: Part1.D4, IC2.In_4
  N5: Part1.D5, IC2.In_3
  N6: Part1.D6, U4.4
  N7: Part1.D7, U4.3
  N8: Part1.VIN, IC2.+Vmotor, S5.leg1
  N9: Part1.5V, IC2.+V, R2.leg1, S4.Pin_3, S4.Pin_4, U4.2
  N10: Part1.A0, R2.wiper
  N11: IC2.Out_3_(_Controlled_by_Enable_2_), M2.pin_2
  N12: IC2.Out_4_(_Controlled_by_Enable_2_), M2.pin_1
  N13: U3.+, S5.leg0
