# Fritzing sketch Tornado (saved by Fritzing 0.9.3b)
breadboards: 1

parts:
  Part1 = Arduino Pro Mini v13
  IC1 = L293D [package=THT]
  R1 = Rotary Potentiometer (Large) [maximum_resistance=100kΩ package=THT]
  S1 = Round Pushbutton
  LED1 = LED - 5mm [color="Red (633nm)" package="5 mm [THT]"]
  LED2 = LED - 5mm [color="Red (633nm)" package="5 mm [THT]"]
  S3 = Pushbutton [package="[THT]"]
  SG1 = Buzzer 12mm [package=buzzer-ccv]
  M1 = DC Motor
  U1 = 7-SEGMENT-4DIGIT [package=7-segment-4digit_longpads_for_pogobed]
  R2 = Resistor [tolerance=±5% resistance=220 package=THT]
  R3 = Resistor [tolerance=±5% resistance=220 package=THT]
  U2 = LIPO-110mAh [package=lipo-110]
  Part2 = Thumb Joystick
  R4 = Resistor [tolerance=±5% resistance=220 package=THT]

nets:
  GND: Part1.GND, IC1.0V, R1.leg1, S1.leg0, LED1.cathode, LED2.cathode, SG1.1, U1.16, R2.Pin_1, Part2.GND
  VCC: Part1.VCC, Part1.D2, IC1.Enable_1, IC1.+Vmotor, R1.leg2, S3.Pin_3, S3.Pin_4, U1.2, U2.+, Part2.VCC
  N1: Part1.A2, Part2.HORZ
  N2: Part1.A1, Part2.VERT
  N3: Part1.A0, R1.wiper
  N4: Part1.D10_PWM/SS, R4.Pin_1
  N5: Part1.D9_PWM, Part2.SEL
  N6: Part1.D8, SG1.2
  N7: Part1.D7, R3.Pin_1
  N8: Part1.D6_PWM, U1.13
  N9: Part1.D5_PWM, U1.15
  N10: Part1.D4, IC1.In_2
  N11: Part1.D3_PWM, IC1.In_1
  N12: IC1.Out_1_(_Controlled_by_Enable_1_), M1.pin_2
  N13: IC1.Out_2_(_Controlled_by_Enable_1_), M1.pin_1
  N14: S1.leg1, U2.-
  N15: LED1.anode, R3.Pin_0
  N16: LED2.anode, R4.Pin_0
  N17: S3.Pin_1, S3.Pin_2, R2.Pin_0
